// Logisim project Arch.circ as structural Verilog: 17 circuits, main circuit main
module main (
  input  Clk,
  input  Rst,
  input  Int,
  input  [15:0] IN_PORT,
  output [15:0] out_5
);

  wire cu_1_is_alu, decode_stage_1_p1, decode_stage_1_p2, memory_buffer_1_out_5, memory_buffer_1_out_6,
       undriven, undriven_2, undriven_3, undriven_4, undriven_5, undriven_6, undriven_7;
  wire [3:0] cu_1_alu_instr;
  wire [4:0] decode_stage_1_p4;
  wire [15:0] decode_stage_1_p5, decode_stage_1_p6, fetch_stage_1_instr;

  Register #(.width(16)) PC ();  // open: D, en, Q, clk, clr
  Register #(.width(16)) SP ();  // open: D, en, Q, clk, clr
  Fetch_Stage fetch_stage_1 (.Clk(Clk), .Instr(fetch_stage_1_instr));  // open: PC
  Register #(.width(16)) OUT_PORT ();  // open: D, en, Q, clk, clr
  Fetch_Buffer fetch_buffer_1 (
    .Clk(Clk), .En(undriven_2), .Rst(undriven), .Instr(fetch_stage_1_instr));  // open: Addr, Full_Instr, Data_1, Data_2, Write_Addr_1, Write_Addr_2
  // Decode_Stage decode_stage_1: pin names not known; wires that end beside it: decode_stage_1_p1, decode_stage_1_p2, Clk, decode_stage_1_p4, decode_stage_1_p5, decode_stage_1_p6
  CU cu_1 (.Opcode(decode_stage_1_p4), .Is_ALU(cu_1_is_alu), .ALU_Instr(cu_1_alu_instr));
  Decode_Buffer decode_buffer_1 (
    .Clk(Clk), .En(decode_stage_1_p1), .Rst(decode_stage_1_p2), .Src(decode_stage_1_p5),
    .Dst(decode_stage_1_p6), .Is_ALU_In(cu_1_is_alu), .ALU_Instr_In(cu_1_alu_instr));  // open: Is_ALU_Out, ALU_Instr_Out, Op1, Op2
  Execute_Stage execute_stage_1 (.Clk(Clk), .Rst(undriven_3));  // open: Is_ALU, ALU_Instr, Op1, Op2, Result
  Execute_Buffer execute_buffer_1 (.Clk(Clk), .En(undriven_5), .Rst(undriven_4));  // open: Result, R_W, Addr, Data
  Memory_Stage memory_stage_1 (.Clk(Clk));  // open: R_W, Addr, Data, Word
  Write_Back_Stage write_back_stage_1 (.Clk(Clk), .in_2(memory_buffer_1_out_5), .in_3(memory_buffer_1_out_6));
  Memory_Buffer memory_buffer_1 (
    .Clk(Clk), .En(undriven_7), .Rst(undriven_6), .out_5(memory_buffer_1_out_5), .out_6(memory_buffer_1_out_6));  // open: Word
  Write_Back_Stage write_back_stage_2 ();  // open: Clk, in_2, in_3
endmodule

module Register_File (
  input  Clk,
  input  [15:0] Data_1,
  input  [15:0] Data_2,
  input  [2:0] Write_Addr_1,
  input  [2:0] Write_Addr_2,
  input  [2:0] Src_Addr,
  input  [2:0] Dst_Addr,
  output [15:0] Src,
  output [15:0] Dst
);

  wire decoder_1_out0, decoder_1_out1, decoder_1_out2, decoder_1_out3, decoder_1_out4, decoder_1_out5,
       decoder_2_out0, decoder_2_out1, decoder_2_out2, decoder_2_out3, decoder_2_out4, decoder_2_out5;
  wire [15:0] double_register_1_q, double_register_2_q, double_register_3_q, double_register_4_q,
       double_register_5_q, double_register_6_q;

  Decoder #(.select(3), .enable("false")) decoder_1 (
    .out0(decoder_1_out0), .out1(decoder_1_out1), .out2(decoder_1_out2), .out3(decoder_1_out3),
    .out4(decoder_1_out4), .out5(decoder_1_out5), .sel(Write_Addr_1));  // open: out6, out7
  Decoder #(.select(3), .enable("false")) decoder_2 (
    .out0(decoder_2_out0), .out1(decoder_2_out1), .out2(decoder_2_out2), .out3(decoder_2_out3),
    .out4(decoder_2_out4), .out5(decoder_2_out5), .sel(Write_Addr_2));  // open: out6, out7
  Double_Register double_register_1 (
    .D1(Data_1), .D2(Data_2), .En_1(decoder_1_out0), .En_2(decoder_2_out0), .Clk(Clk), .Q(double_register_1_q));
  Double_Register double_register_2 (
    .D1(Data_1), .D2(Data_2), .En_1(decoder_1_out3), .En_2(decoder_2_out3), .Clk(Clk), .Q(double_register_2_q));
  Multiplexer #(.select(3), .width(16), .enable("false")) multiplexer_1 (
    .in0(double_register_1_q), .in1(double_register_2_q), .in2(double_register_3_q),
    .in3(double_register_4_q), .in4(double_register_5_q), .in5(double_register_6_q), .out(Src), .sel(Src_Addr));  // open: in6, in7
  Double_Register double_register_3 (
    .D1(Data_1), .D2(Data_2), .En_1(decoder_1_out1), .En_2(decoder_2_out1), .Clk(Clk), .Q(double_register_3_q));
  Double_Register double_register_4 (
    .D1(Data_1), .D2(Data_2), .En_1(decoder_1_out4), .En_2(decoder_2_out4), .Clk(Clk), .Q(double_register_4_q));
  Multiplexer #(.select(3), .width(16), .enable("false")) multiplexer_2 (
    .in0(double_register_1_q), .in1(double_register_2_q), .in2(double_register_3_q),
    .in3(double_register_4_q), .in4(double_register_5_q), .in5(double_register_6_q), .out(Dst), .sel(Dst_Addr));  // open: in6, in7
  Double_Register double_register_5 (
    .D1(Data_1), .D2(Data_2), .En_1(decoder_1_out2), .En_2(decoder_2_out2), .Clk(Clk), .Q(double_register_5_q));
  Double_Register double_register_6 (
    .D1(Data_1), .D2(Data_2), .En_1(decoder_1_out5), .En_2(decoder_2_out5), .Clk(Clk), .Q(double_register_6_q));
endmodule

module Fetch_Stage (
  input  Clk,
  input  [8:0] PC,
  output [15:0] Instr
);

  wire [8:0] undriven;

  Instr_RAM instr_ram_1 (.Clk(Clk), .Addr(undriven), .Instr(Instr));
endmodule

module Decode_Stage (
  input  Clk,
  input  [15:0] Full_Instr,
  input  [15:0] Data_1,
  input  [15:0] Data_2,
  input  [2:0] Write_Addr_1,
  input  [2:0] Write_Addr_2,
  output [4:0] Opcode,
  output [15:0] Src,
  output [15:0] Dst
);

  Register_File register_file_1 (
    .Clk(Clk), .Data_1(Data_1), .Data_2(Data_2), .Write_Addr_1(Write_Addr_1), .Write_Addr_2(Write_Addr_2),
    .Src_Addr(Full_Instr[10:8]), .Dst_Addr(Full_Instr[7:5]), .Src(Src), .Dst(Dst));

  assign Opcode = Full_Instr[15:11];
endmodule

module Execute_Stage (
  input  Clk,
  input  Rst,
  input  Is_ALU,
  input  [3:0] ALU_Instr,
  input  [15:0] Op1,
  input  [15:0] Op2,
  output [31:0] Result
);

  wire not_1_out;
  wire [3:0] alu_1_flags, CCR_q;
  wire [15:0] alu_1_result;
  wire [31:0] bit_extender_1_out, multip_1_result;

  Register #(.width(4)) CCR (.D(alu_1_flags), .en(Is_ALU), .clk(Clk), .Q(CCR_q), .clr(Rst));
  ALU alu_1 (.ALU_Instr(ALU_Instr), .Op1(Op1), .Op2(Op2), .C_In(CCR_q[2]), .Result(alu_1_result), .Flags(alu_1_flags));
  assign bit_extender_1_out = {{16{alu_1_result[15]}}, alu_1_result};  // Bit_Extender bit_extender_1
  Multip multip_1 (.Op1(Op1), .Op2(Op2), .Result(multip_1_result));
  not not_1 (not_1_out, Is_ALU);
  Multiplexer #(.width(32), .enable("false")) multiplexer_1 (
    .in0(bit_extender_1_out), .in1(multip_1_result), .out(Result), .sel(not_1_out));
endmodule

module Memory_Stage (
  input  Clk,
  input  R_W,
  input  [8:0] Addr,
  input  [15:0] Data,
  output [15:0] Word
);

  Data_RAM data_ram_1 (.Clk(Clk), .R_W(R_W), .Addr(Addr), .Data_In(Data), .Data_Out(Word));
endmodule

module Write_Back_Stage (
  input  Clk,
  input  in_2,
  input  in_3
);
endmodule

module Instr_RAM (
  input  Clk,
  input  [8:0] Addr,
  output [15:0] Instr
);
endmodule

module Double_Register (
  input  [15:0] D1,
  input  [15:0] D2,
  input  En_1,
  input  En_2,
  input  Clk,
  output [15:0] Q
);

  wire or_1_out;
  wire [15:0] multiplexer_1_out;

  Register #(.width(16)) register_1 (.D(multiplexer_1_out), .en(or_1_out), .clk(Clk), .Q(Q));  // open: clr
  Multiplexer #(.width(16), .enable("false")) multiplexer_1 (.in0(D1), .in1(D2), .out(multiplexer_1_out), .sel(En_2));
  or or_1 (or_1_out, En_1, En_2);
endmodule

module CU (
  input  [4:0] Opcode,
  output Is_ALU,
  output [3:0] ALU_Instr
);
endmodule

module ALU (
  input  [3:0] ALU_Instr,
  input  [15:0] Op1,
  input  [15:0] Op2,
  input  C_In,
  output [15:0] Result,
  output [3:0] Flags
);
endmodule

module Multip (
  input  [15:0] Op1,
  input  [15:0] Op2,
  output [31:0] Result
);
endmodule

module Data_RAM (
  input  Clk,
  input  R_W,
  input  [8:0] Addr,
  input  [15:0] Data_In,
  output [15:0] Data_Out
);
endmodule

module Fetch_Buffer (
  input  Clk,
  input  En,
  input  Rst,
  input  [15:0] Instr,
  input  [15:0] Addr,
  output [15:0] Full_Instr,
  output [15:0] Data_1,
  output [15:0] Data_2,
  output [2:0] Write_Addr_1,
  output [2:0] Write_Addr_2
);
endmodule

module Decode_Buffer (
  input  Clk,
  input  En,
  input  Rst,
  input  [15:0] Src,
  input  [15:0] Dst,
  input  Is_ALU_In,
  input  [3:0] ALU_Instr_In,
  output Is_ALU_Out,
  output [3:0] ALU_Instr_Out,
  output [15:0] Op1,
  output [15:0] Op2
);
endmodule

module Execute_Buffer (
  input  Clk,
  input  En,
  input  Rst,
  input  [31:0] Result,
  output R_W,
  output [8:0] Addr,
  output [15:0] Data
);
endmodule

module Memory_Buffer (
  input  Clk,
  input  En,
  input  Rst,
  input  [15:0] Word,
  output out_5,
  output out_6
);
endmodule
